# Fritzing sketch trinket_rfm69 (saved by Fritzing 0.9.3b)

parts:
  Part1 = Adafruit Trinket 3V [part_number="Adafruit #1500"]
  RFM1 = RFM69HCW ISM Transciever

nets:
  N1: Part1.#4, RFM1.14_DIO0
  N2: Part1.#3, RFM1.5_NSS_(CS)
  N3: Part1.#0, RFM1.2_MISO
  N4: Part1.#1, RFM1.3_MOSI
  N5: Part1.#2, RFM1.4_SCK

notes:
  Antenna
  To Supply 3.3V
  To Supply GND

custom parts:
  Adafruit Trinket 3V: Trinket may be small, but do not be fooled by its size! It's a tiny microcontroller board, built around the Atmel ATtiny85, a little chip with a lot of power. We wanted to design a microcontroller board that was small enough to fit into any project, and low cost enough to use without hesitation. Perfect for when you don't want to give up your expensive dev-board and you aren't willing to take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
  RFM69HCW ISM Transciever: RF Transceiver by Hope RF. Well supported Arduino libraries are available. This ISM band transceiver is available in several frequencies e.g. 433MHz and 915MHz and it is also available in various feature versions.
